# Fritzing sketch hardware_layout_v0.1 (saved by Fritzing 0.9.3b)
breadboards: 1

parts:
  Raspberry_Pi_1 = Raspberry Pi 3 [part_number=RPI-3-V1.2]
  S1 = Pushbutton [package="[THT]"]
  S2 = Taiway 100-SP-X-T1 SPDT Miniature Toggle Switch [part_number=100-SP-X-T1-0-0-B1-M1 package=THT]

nets:
  N1: Raspberry_Pi_1.GND, S1.Pin_4, S2.L2
  N2: Raspberry_Pi_1.GIPO27, S1.Pin_2
  N3: Raspberry_Pi_1.GIPO19, S2.L1
